# Fritzing sketch sensorbox (saved by Fritzing 0.9.4)

parts:
  U1 = NodeMCU V3.0
  Bauteil1 = BH1750
  DHT1 = AM2302 DHT22 Humidity and Temperature Sensor
  AM312 = PIR sensor

nets:
  N1: U1.D1, AM312.SIG
  N2: U1.D2, Bauteil1.SDA
  N3: U1.D3, Bauteil1.SCL
  VCC: U1.3V3, Bauteil1.VCC, DHT1.VCC, AM312.VDD
  GND: U1.GND, Bauteil1.GND, DHT1.GND, AM312.GND
  N4: U1.D6, DHT1.DAT

custom parts:
  NodeMCU V3.0: ESP8266 based NodeMCU
  BH1750: Light Sensor
